# Fritzing sketch ShrimPCB-gnd (saved by Fritzing 0.7.11b)
breadboards: 1

parts:
  U1 = atmega168 [package=dip]
  C1 = Electrolytic Capacitor [capacitance=10µF package="100 mil [THT, electrolytic]"]
  C2 = Ceramic Capacitor [capacitance=100nF package="100 mil [THT, multilayer]"]
  C3 = Ceramic Capacitor [capacitance=100nF package="100 mil [THT, multilayer]"]
  R1 = Resistor [tolerance=±5% resistance=100k package=THT]
  D1 = Rectifier Diode [part_number=1N4001 package="300 mil [THT]"]
  C4 = Ceramic Capacitor [capacitance=100nF package="100 mil [THT, multilayer]"]
  C5 = Ceramic Capacitor [capacitance=22µF package="100 mil [THT, multilayer]"]
  C6 = Ceramic Capacitor [capacitance=22µF package="100 mil [THT, multilayer]"]
  XTAL = Crystal [frequency="16 Mhz" package=THT]
  C7 = Ceramic Capacitor [capacitance=100nF package="100 mil [THT, multilayer]"]
  S1 = Pushbutton [package="[THT]"]
  J3 = female pin header, 5 pins [form="♀ (female)"]
  J4 = shrouded pin header, 6 pins [form="♂ (shrouded male)"]
  J2 = female pin header, 14 pins [form="♀ (female)"]
  J1 = female pin header, 14 pins [form="♀ (female)"]
  PWRLED = LED - 5mm [color="Red (633nm)" package="5 mm [THT]"]
  R5 = Resistor [tolerance=±5% resistance=220 package=THT]
  R6 = Resistor [tolerance=±5% resistance=220 package=THT]
  P13LED = LED - 5mm [color="Red (633nm)" package="5 mm [THT]"]

nets (from the pcb view):
  N1: U1.RESET, R1.Pin_0, D1.cathode, C7.1, S1.Pin_3, S1.Pin_4, J1.pin14
  N2: U1.D0_(RX), J3.pin4, J1.pin13
  N3: U1.D1_(TX), J3.pin3, J1.pin12
  N4: U1.D2, J1.pin11
  N5: U1.D3_(PWM), J1.pin10
  N6: U1.D4, J1.pin9
  N7: U1.VCC, U1.AVCC, C1.+, C3.1, R1.Pin_1, D1.anode, C4.0, J4.pin6, J2.pin6, J1.pin8
  N8: U1.GND#7, C4.1, C5.0, C6.0, S1.Pin_1, S1.Pin_2, J1.pin7
  N9: U1.XLAT1, C5.1, XTAL.pin_0, J1.pin6
  N10: U1.XLAT2, C6.1, XTAL.pin_1, J1.pin5
  N11: U1.D5_(PWM), J1.pin4
  N12: U1.D6_(PWM), J1.pin3
  N13: U1.D7, J1.pin2
  N14: U1.D8, J1.pin1
  N15: U1.D9_(PWM), J2.pin1
  N16: U1.D10_(PWM), J2.pin2
  N17: U1.D11_(PWM), J4.pin5, J2.pin3
  N18: U1.D12, J4.pin1, J2.pin4
  N19: U1.D13, J4.pin2, J2.pin5, R6.Pin_1
  N20: U1.AREF, C2.1, J2.pin7
  N21: U1.GND#21, C1.-, C2.0, C3.0, J3.pin5, J4.pin4, J2.pin8, R5.Pin_1, P13LED.cathode
  N22: U1.A0, J2.pin9
  N23: U1.A1, J2.pin10
  N24: U1.A2, J2.pin11
  N25: U1.A3, J2.pin12
  N26: U1.A4, J2.pin13
  N27: U1.A5, J2.pin14
  N28: C7.0, J3.pin1
  N29: J3.pin2, PWRLED.anode
  N30: PWRLED.cathode, R5.Pin_0
  N31: R6.Pin_0, P13LED.anode
